// Logisim project ALU.circ as structural Verilog: 1 circuit, main circuit ALU
module ALU (
  input  [31:0] A,
  input  [31:0] B,
  input  [3:0] Codop,
  input  [4:0] Shift,
  input  CarryIn,
  output [31:0] S,
  output [3:0] Flags
);

  wire [31:0] ADC, AND, ASR, BIC, EOR, LSL, LSR, MUL, MVN, not_1_out, ORR, ROR, SBC;

  assign AND = A & B;  // AND_Gate and_1, 32 bits wide
  assign EOR = A ^ B;  // XOR_Gate xor_1, 32 bits wide
  Shifter #(.width(32)) shifter_1 (.in(B), .\dist (Shift), .out(LSL));
  Shifter #(.width(32), .shift("lr")) shifter_2 (.in(B), .\dist (Shift), .out(LSR));
  Shifter #(.width(32), .shift("ar")) shifter_3 (.in(B), .\dist (Shift), .out(ASR));
  Adder #(.width(32)) adder_1 (.a(A), .b(B), .out(ADC), .cin(CarryIn));  // open: cout
  Subtractor #(.width(32)) subtractor_1 (.a(A), .b(B), .out(SBC), .bin(CarryIn));  // open: bout
  Shifter #(.width(32), .shift("rr")) shifter_4 (.in(A), .\dist (Shift), .out(ROR));
  Multiplexer #(.select(4), .width(32), .enable("false")) multiplexer_1 (
    .in0(AND), .in1(EOR), .in2(LSL), .in3(LSR), .in4(ASR), .in5(ADC), .in6(SBC), .in7(ROR), .in8(B),
    .in10(B), .in11(B), .in12(ORR), .in13(MUL), .in14(BIC), .in15(MVN));  // open: in9, out, sel
  assign ORR = A | B;  // OR_Gate or_1, 32 bits wide
  Multiplier #(.width(32)) multiplier_1 (.a(A), .b(B), .out(MUL));  // open: cin, cout
  assign BIC = A & not_1_out;  // AND_Gate and_2, 32 bits wide
  assign not_1_out = ~B;  // NOT_Gate not_1, 32 bits wide
  assign MVN = ~B;  // NOT_Gate not_2, 32 bits wide

  // Other names for the same wires on the sheet: N = Flags[0]; Z = Flags[1]; C = Flags[2]; V = Flags[3];
  //   CMN[31:0] = B; CMP[31:0] = B; TST[31:0] = B

  // Notes on the sheet:
  //   Note: for ROR, C = N
  //   Note 2: assume that shift > 0 for LSL and LSR
endmodule
